# Fritzing sketch potentiometer_led (saved by Fritzing 0.9.2b)
breadboards: 1

parts:
  Part1 = Arduino Uno (Rev3) - ICSP
  R1 = Rotary Potentiometer (Small) [maximum_resistance=100kΩ package=THT]
  LED1 = smd LED [color="Red (633nm)" package="0603 [SMD]"]
  R2 = Resistor [tolerance=±5% resistance=220 package="2010 [SMD]"]

nets:
  N1: Part1.A0, R1.wiper
  N2: Part1.D5_PWM, R2.Pin_1
  N3: Part1.5V, R1.leg2
  N4: Part1.GND, R1.leg1, LED1.anode
  N5: LED1.cathode, R2.Pin_0
