# Fritzing sketch potentiometer_servo_button (saved by Fritzing 0.9.2b)
breadboards: 1

parts:
  Part1 = Arduino Uno (Rev3) - ICSP
  R1 = Rotary Potentiometer (Small) [maximum_resistance=100kΩ package=THT]
  LED1 = smd LED [color="Red (633nm)" package="0603 [SMD]"]
  R2 = Resistor [tolerance=±5% resistance=220 package="2010 [SMD]"]
  J1 = Basic Servo
  S1 = Momentary Switch [package=ksa_sealed_tac_switch]

nets:
  N1: Part1.A0, R1.wiper
  GND: Part1.GND, R1.leg1, LED1.anode, J1.gnd, S1.2
  N2: Part1.D2, S1.4
  N3: Part1.D5_PWM, R2.Pin_1
  N4: Part1.D6_PWM, J1.pulse
  5V: Part1.5V, R1.leg2, J1.vcc
  N5: LED1.cathode, R2.Pin_0
